# Fritzing sketch Button_diode_IOREF (saved by Fritzing 0.9.3b)
breadboards: 1

parts:
  Часть1 = Arduino Uno (Rev3)
  R1 = Resistor [tolerance=±5% resistance=220 package=THT]
  S1 = Pushbutton [package="[THT]"]

nets:
  N1: Часть1.D7, R1.Pin_1, S1.Pin_3, S1.Pin_4
  N2: Часть1.ioref, R1.Pin_0
  N3: Часть1.GND, S1.Pin_1, S1.Pin_2

// code stored in the sketch: Button_diode_IOREF1.ino
int ledPin = 13; // choose the pin for the LED
int inPin = 7;   // choose the input pin (for a pushbutton)
int val = 0;     // variable for reading the pin status

void setup() {
  pinMode(ledPin, OUTPUT);  // declare LED as output
  pinMode(inPin, INPUT);    // declare pushbutton as input
}

void loop(){
  val = digitalRead(inPin);  // read input value
  if (val == HIGH) {         // check if the input is HIGH (button released)
    digitalWrite(ledPin, LOW);  // turn LED OFF
  } else {
    digitalWrite(ledPin, HIGH);  // turn LED ON
  }
}
