# Fritzing sketch Untitled Sketch 3 (saved by Fritzing 0.9.3b)
breadboards: 1

parts:
  Часть1 = Arduino Uno (Rev3)
  D1 = LED_BARGRAPH_10 [package=led_bargaph_10]
  R1 = Resistor [tolerance=±5% resistance=220 package=THT]

nets:
  N1: Часть1.3V3, D1.B_C, D1.A_C, R1.Pin_0
  N2: Часть1.GND, D1.A_A, D1.B_A
  N3: D1.E_C, R1.Pin_1
